# Fritzing sketch circuit (saved by Fritzing 0.8.7b)
breadboards: 1

parts:
  part = Arduino Leonardo (Rev3b)
  Bluetooth = IC, SIP package, 6 pins [chip_label=HC05]
  R1 = Resistor [tolerance=±5% resistance=1k package="1206 [SMD]"]
  R2 = Resistor [tolerance=±5% resistance=2k package="0805 [SMD]"]
  J1 = Basic Servo
  LED1 = LED - 5mm [color="Green (565nm)" package="5 mm [THT]"]
  LED2 = LED - 5mm [color="Red (633nm)" package="5 mm [THT]"]
  R3 = Resistor [tolerance=±5% resistance=220 package=THT]
  R4 = Resistor [tolerance=±5% resistance=220 package=THT]
  SG1 = Buzzer 12mm [package=buzzer-ccv-kit]

nets:
  N1: part.D0/RX, Bluetooth.pin4
  N2: part.D1/TX, R1.Pin_0
  N3: part.D4/A6, R4.Pin_0
  N4: part.D5_PWM, SG1.1
  N5: part.3V3, Bluetooth.pin5
  5V: part.5V, J1.vcc
  N6: part.SDA, J1.pulse
  N7: part.SCL, R3.Pin_0
  N8: Bluetooth.pin3, R1.Pin_1, R2.Pin_0
  GND: Bluetooth.pin6, R2.Pin_1, J1.gnd, LED1.cathode, LED2.cathode, SG1.2
  N9: LED1.anode, R3.Pin_1
  N10: LED2.anode, R4.Pin_1
